// Logisim project mainProgram.circ as structural Verilog
module DataPath (
);

  wire AluSrc, Cin, Clear_out, Clock, controlunit_1_p6, Cout, ExtOP, JAL, Jump, JumpRegister, LUI, main_1_p6,
       MemRead, MemToReg, MemWrite, PCSrc, RegDst0, RegDst1, RegDst7, RegWrite, sltFlag, ZFlag;
  wire [1:0] aluSelector, Func, opSelector;
  wire [2:0] multiplexer_1_out, multiplexer_2_out, multiplexer_3_out, Rd, Rs, Rt;
  wire [4:0] Opcode;
  wire [15:0] adder_1_out, AluResult, bit_extender_1_out, bit_extender_2_out, BusA, BusB, BusW, Data_Out,
       multiplexer_4_out, multiplexer_5_out, multiplexer_6_out, multiplexer_7_out, PC, R1, R2, R3, R4, R5,
       R6, R7;

  Clock clock_1 (.out(Clock));
  // PC pc_1: pin names not known; wires that end beside it: {Func, Rd, Rs, Rt}, BusA, Clock, PCSrc, Jump, JumpRegister, PC
  // controlUnit controlunit_1: pin names not known; wires that end beside it: Opcode, Func, ZFlag, sltFlag, RegDst0, controlunit_1_p6, RegDst1, RegDst7, AluSrc
  Button button_1 (.out(controlunit_1_p6));
  ROM #(.addrWidth(16), .dataWidth(16)) rom_1 (.addr(PC), .data({Opcode, Func, Rd, Rs, Rt}), .sel(1'b1));
  Multiplexer #(.width(3), .enable("false")) multiplexer_1 (.in0(Rt), .in1(Rd), .out(multiplexer_1_out), .sel(RegDst0));
  Multiplexer #(.width(3), .enable("false")) multiplexer_2 (
    .in0(multiplexer_1_out), .in1(3'b001), .out(multiplexer_2_out), .sel(RegDst1));
  // Probe on R7
  // Probe on R6
  // Probe on R5
  // Probe on R4
  // Probe on R3
  // Probe on R2
  // Probe on R1
  Multiplexer #(.width(3), .enable("false")) multiplexer_3 (
    .in0(multiplexer_2_out), .in1(3'b111), .out(multiplexer_3_out), .sel(RegDst7));
  Button Clear (.out(Clear_out));
  // RF rf_1: pin names not known; wires that end beside it: R2, Clock, R3, R4, Clear_out, R5, R6, RegWrite, R7, BusA, BusB, BusW
  assign bit_extender_1_out = {{11{1'b0}}, {Func, Rd}};  // Bit_Extender bit_extender_1
  assign bit_extender_2_out = {{11{Func[1]}}, {Func, Rd}};  // Bit_Extender bit_extender_2
  Multiplexer #(.width(16), .enable("false")) multiplexer_4 (
    .in0(bit_extender_1_out), .in1(bit_extender_2_out), .out(multiplexer_4_out), .sel(ExtOP));
  Multiplexer #(.width(16), .enable("false")) multiplexer_5 (
    .in0(BusB), .in1(multiplexer_4_out), .out(multiplexer_5_out), .sel(AluSrc));
  Multiplexer #(.width(16), .enable("false")) multiplexer_6 (
    .in0(AluResult), .in1(Data_Out), .out(multiplexer_6_out), .sel(MemToReg));
  // ALU alu_1: pin names not known; wires that end beside it: BusA, multiplexer_5_out, Cin, opSelector, Cout, aluSelector, AluResult, sltFlag, ZFlag
  Multiplexer #(.width(16), .enable("false")) multiplexer_7 (
    .in0(multiplexer_6_out), .in1({Func, Rd, Rs, Rt, {5{1'b0}}}), .out(multiplexer_7_out), .sel(LUI));
  Adder #(.width(16)) adder_1 (.a(PC), .b(16'h1), .out(adder_1_out), .cin(1'b0));  // open: cout
  Multiplexer #(.width(16), .enable("false")) multiplexer_8 (
    .in0(multiplexer_7_out), .in1(adder_1_out), .out(BusW), .sel(JAL));
  // Data_Memory_main main_1: pin names not known; wires that end beside it: AluResult, BusB, MemRead, Clock, MemWrite, main_1_p6, Data_Out
  Button button_2 (.out(main_1_p6));
endmodule
